# Fritzing sketch Photoresistor Tutorial (saved by Fritzing 0.9.3b)
breadboards: 1

parts:
  R1 = PHOTOCELL [package=photocell]
  Part1 = Arduino Uno (Rev3)
  R6 = Resistor [tolerance=±5% resistance=220 package=THT]

nets:
  N1: R1.P$1, Part1.5V
  N2: R1.P$2, Part1.A0, R6.Pin_0
  N3: Part1.GND, R6.Pin_1
