# Fritzing sketch Piezo with PIR Sensor Tutorial (saved by Fritzing 0.9.3b)
breadboards: 1

parts:
  Part1 = Arduino Uno (Rev3)
  J1 = Piezo Speaker
  Q1 = NPN-Transistor [package="TO92 [THT]"]
  R1 = Resistor [tolerance=±5% resistance=220 package=THT]

nets:
  N1: Part1.D9_PWM, R1.Pin_0
  N2: Part1.GND, Q1.E
  N3: Part1.5V, J1.pin2
  N4: J1.pin1, Q1.C
  N5: Q1.B, R1.Pin_1
