# Fritzing sketch Piezo Tutorial (saved by Fritzing 0.9.3b)
breadboards: 1

parts:
  Part1 = Arduino Uno (Rev3)
  J1 = Piezo Speaker
  Q1 = TRANSISTOR_PNP [package=to-92]
  R1 = Resistor [tolerance=±5% resistance=220 package=THT]

nets:
  N1: Part1.D9_PWM, R1.Pin_1
  N2: Part1.5V, J1.pin1
  N3: Part1.GND, Q1.C
  N4: J1.pin2, Q1.E
  N5: Q1.B, R1.Pin_0
