# Fritzing sketch Ping-3U (saved by Fritzing 0.9.3b)
breadboards: 1

parts:
  Part1 = Arduino Uno (Rev3)
  hc-sr1 = hc-sr04
  hc-sr2 = hc-sr04
  hc-sr3 = hc-sr04

nets:
  N1: Part1.D8, hc-sr3.Echo
  N2: Part1.D9_PWM, hc-sr3.Trig
  N3: Part1.D10_PWM/SS, hc-sr2.Echo
  N4: Part1.D11_PWM/MOSI, hc-sr2.Trig
  N5: Part1.D12/MISO, hc-sr1.Echo
  N6: Part1.D13/SCK, hc-sr1.Trig
  GND: Part1.GND, hc-sr1.GND, hc-sr2.GND, hc-sr3.GND
  VCC: Part1.5V, hc-sr1.VCC, hc-sr2.VCC, hc-sr3.VCC
