# Fritzing sketch TCRT Touch 1 (saved by Fritzing 0.9.3b)
breadboards: 1

parts:
  Part1 = Arduino Uno (Rev3)
  R1 = Resistor [tolerance=±5% resistance=10k package=THT]
  R2 = Resistor [tolerance=±5% resistance=100 package=THT]
  LED1 = LED - 5mm [color="Blue (470nm)" package="5 mm [THT]"]
  LED2 = LED - 5mm [color="Infrared (850nm)" package="5 mm [THT]"]

nets:
  N1: Part1.A0, R1.Pin_1, LED2.anode
  N2: Part1.5V, R1.Pin_0, R2.Pin_1
  N3: Part1.GND, LED1.anode, LED2.cathode
  N4: R2.Pin_0, LED1.cathode
