# Fritzing sketch Themistor Tutorial (saved by Fritzing 0.9.3b)
breadboards: 1

parts:
  R1 = Temperature Sensor (Thermistor) [thermistor_type=NTC package=THT]
  Part1 = Arduino Uno (Rev3)
  R2 = Resistor [tolerance=±5% resistance=220 package=THT]

nets:
  N1: R1.pin_0, Part1.A0, R2.Pin_0
  N2: R1.pin_1, Part1.5V
  N3: Part1.GND, R2.Pin_1
