# Fritzing sketch Fritzing-Sonar_Tutorial (saved by Fritzing 0.9.3b)
breadboards: 1

parts:
  Part1 = Arduino Uno (Rev3)
  J1 = Basic Servo
  hc-sr1 = hc-sr04

nets:
  N1: Part1.D9_PWM, hc-sr1.Trig
  N2: Part1.D10_PWM/SS, hc-sr1.Echo
  N3: Part1.D12/MISO, J1.pulse
  GND: Part1.GND, J1.gnd, hc-sr1.GND
  VCC: Part1.5V, J1.vcc, hc-sr1.VCC
